// Logisim project LAB3 PART2.circ as structural Verilog: 4 circuits, main circuit main
module main (
  input  A,
  input  B,
  input  C,
  output out_4
);

  wire n4075_or_1_out_10, n4075_or_1_out_11, n4075_or_1_out_12, n4075_or_2_out_10, n4075_or_2_out_11,
       n7404_not_1_out_10, n7404_not_1_out_11, n7404_not_1_out_12, n7411_and_1_out_10;

  _7404_NOT u_7404_not_1 (
    .in_4(A), .in_5(C), .in_6(B), .out_10(n7404_not_1_out_10), .out_11(n7404_not_1_out_11),
    .out_12(n7404_not_1_out_12));  // open: in_1, in_2, in_3, out_7, out_8, out_9
  _4075_OR u_4075_or_1 (
    .in_1(A), .in_2(B), .in_3(C), .in_4(A), .in_5(n7404_not_1_out_12), .in_6(n7404_not_1_out_11),
    .in_7(n7404_not_1_out_10), .in_8(B), .in_9(C), .out_10(n4075_or_1_out_10), .out_11(n4075_or_1_out_11),
    .out_12(n4075_or_1_out_12));
  _4075_OR u_4075_or_2 (
    .in_1(n7404_not_1_out_10), .in_2(C), .in_3(C), .in_4(n7404_not_1_out_10), .in_5(n7404_not_1_out_12),
    .in_6(n7404_not_1_out_11), .out_10(n4075_or_2_out_10), .out_11(n4075_or_2_out_11));  // open: in_7, in_8, in_9, out_12
  _7411_AND u_7411_and_1 (
    .in_1(n4075_or_1_out_10), .in_2(n4075_or_1_out_11), .in_3(n4075_or_1_out_12), .in_4(n4075_or_2_out_10),
    .in_5(n4075_or_2_out_11), .in_6(n7411_and_1_out_10), .out_10(n7411_and_1_out_10), .out_11(out_4));  // open: in_7, in_8, in_9, out_12
endmodule

module _7411_AND (
  input  in_1,
  input  in_2,
  input  in_3,
  input  in_4,
  input  in_5,
  input  in_6,
  input  in_7,
  input  in_8,
  input  in_9,
  output out_10,
  output out_11,
  output out_12
);

  and and_1 (out_10, in_1, in_2, in_3);
  and and_2 (out_11, in_4, in_5, in_6);
  and and_3 (out_12, in_7, in_8, in_9);
endmodule

module _4075_OR (
  input  in_1,
  input  in_2,
  input  in_3,
  input  in_4,
  input  in_5,
  input  in_6,
  input  in_7,
  input  in_8,
  input  in_9,
  output out_10,
  output out_11,
  output out_12
);

  or or_1 (out_10, in_1, in_2, in_3);
  or or_2 (out_11, in_4, in_5, in_6);
  or or_3 (out_12, in_7, in_8, in_9);
endmodule

module _7404_NOT (
  input  in_1,
  input  in_2,
  input  in_3,
  input  in_4,
  input  in_5,
  input  in_6,
  output out_7,
  output out_8,
  output out_9,
  output out_10,
  output out_11,
  output out_12
);

  not not_1 (out_7, in_1);
  not not_2 (out_8, in_2);
  not not_3 (out_9, in_3);
  not not_4 (out_10, in_4);
  not not_5 (out_11, in_5);
  not not_6 (out_12, in_6);
endmodule
