// Logisim project WEEK4 LAB4.circ as structural Verilog: 4 circuits, main circuit main
module main (
  input  W,
  input  X,
  input  Y,
  input  Z,
  output B,
  output A,
  output C,
  output D
);

  wire and_gate_1_out_9, and_gate_1_out_10, and_gate_1_out_11, and_gate_1_out_12, and_gate_2_out_9,
       and_gate_2_out_10, and_gate_2_out_11, and_gate_2_out_12, or_gate_1_out_9, or_gate_1_out_10,
       or_gate_1_out_11, or_gate_1_out_12, or_gate_2_out_12, undriven;

  NOT_GATE not_gate_1 (
    .in_4(D), .in_5(and_gate_2_out_12), .in_6(undriven), .out_10(Z), .out_11(Y), .out_12(X));  // open: in_1, in_2, in_3, out_7, out_8, out_9
  AND_GATE and_gate_1 (
    .in_1(Z), .in_2(undriven), .in_3(Y), .in_5(Y), .in_6(X), .in_7(Z), .in_8(X), .out_9(and_gate_1_out_9),
    .out_10(and_gate_1_out_10), .out_11(and_gate_1_out_11), .out_12(and_gate_1_out_12));  // open: in_4
  AND_GATE and_gate_2 (
    .in_1(D), .in_2(and_gate_2_out_12), .in_3(Z), .in_4(Y), .in_5(D), .in_7(and_gate_2_out_12), .in_8(X),
    .out_9(and_gate_2_out_9), .out_10(and_gate_2_out_10), .out_11(and_gate_2_out_11),
    .out_12(and_gate_2_out_12));  // open: in_6
  OR_GATE or_gate_1 (
    .in_1(and_gate_1_out_9), .in_2(and_gate_1_out_10), .in_3(or_gate_1_out_9), .in_4(and_gate_2_out_11),
    .in_5(and_gate_1_out_11), .in_6(or_gate_1_out_12), .in_7(and_gate_1_out_12), .in_8(W),
    .out_9(or_gate_1_out_9), .out_10(or_gate_1_out_10), .out_11(or_gate_1_out_11), .out_12(or_gate_1_out_12));
  OR_GATE or_gate_2 (
    .in_7(and_gate_2_out_10), .in_8(and_gate_2_out_9), .out_12(or_gate_2_out_12));  // open: in_1, in_2, in_3, in_4, in_5, in_6, out_9, out_10, out_11
endmodule

module AND_GATE (
  input  in_1,
  input  in_2,
  input  in_3,
  input  in_4,
  input  in_5,
  input  in_6,
  input  in_7,
  input  in_8,
  output out_9,
  output out_10,
  output out_11,
  output out_12
);

  and and_1 (out_9, in_1, in_2);
  and and_2 (out_10, in_3, in_4);
  and and_3 (out_11, in_5, in_6);
  and and_4 (out_12, in_7, in_8);
endmodule

module OR_GATE (
  input  in_1,
  input  in_2,
  input  in_3,
  input  in_4,
  input  in_5,
  input  in_6,
  input  in_7,
  input  in_8,
  output out_9,
  output out_10,
  output out_11,
  output out_12
);

  or or_1 (out_9, in_1, in_2);
  or or_2 (out_10, in_3, in_4);
  or or_3 (out_11, in_5, in_6);
  or or_4 (out_12, in_7, in_8);
endmodule

module NOT_GATE (
  input  in_1,
  input  in_2,
  input  in_3,
  input  in_4,
  input  in_5,
  input  in_6,
  output out_7,
  output out_8,
  output out_9,
  output out_10,
  output out_11,
  output out_12
);

  not not_1 (out_7, in_1);
  not not_2 (out_8, in_2);
  not not_3 (out_9, in_3);
  not not_4 (out_10, in_4);
  not not_5 (out_11, in_5);
  not not_6 (out_12, in_6);
endmodule
