// Logisim project WEEK4LAB4 ().circ as structural Verilog: 4 circuits, main circuit main
module main (
  input  W,
  input  X,
  input  Y,
  input  Z,
  output B,
  output A,
  output C,
  output D
);

  wire and_gate_1_out_9, and_gate_1_out_10, and_gate_1_out_11, and_gate_1_out_12, and_gate_2_out_9,
       and_gate_2_out_10, and_gate_2_out_11, and_gate_2_out_12, not_gate_1_out_11, not_gate_1_out_12,
       or_gate_1_out_9, or_gate_1_out_12;

  AND_GATE and_gate_1 (
    .in_1(not_gate_1_out_12), .in_2(X), .in_3(not_gate_1_out_12), .in_4(Y), .in_5(X), .in_6(Y), .in_7(X),
    .in_8(X), .out_9(and_gate_1_out_9), .out_10(and_gate_1_out_10), .out_11(and_gate_1_out_11),
    .out_12(and_gate_1_out_12));
  NOT_GATE not_gate_1 (
    .in_4(X), .in_5(Y), .in_6(X), .out_10(C), .out_11(not_gate_1_out_11), .out_12(not_gate_1_out_12));  // open: in_1, in_2, in_3, out_7, out_8, out_9
  OR_GATE or_gate_1 (
    .in_1(and_gate_1_out_9), .in_2(and_gate_1_out_10), .in_3(or_gate_1_out_9), .in_4(and_gate_2_out_11),
    .in_5(or_gate_1_out_12), .in_6(and_gate_1_out_11), .in_7(W), .in_8(and_gate_1_out_12),
    .out_9(or_gate_1_out_9), .out_10(B), .out_11(A), .out_12(or_gate_1_out_12));
  AND_GATE and_gate_2 (
    .in_1(not_gate_1_out_11), .in_2(C), .in_3(Y), .in_4(X), .in_5(and_gate_2_out_12), .in_6(C), .in_7(X),
    .in_8(not_gate_1_out_11), .out_9(and_gate_2_out_9), .out_10(and_gate_2_out_10),
    .out_11(and_gate_2_out_11), .out_12(and_gate_2_out_12));
  OR_GATE or_gate_2 (
    .in_7(and_gate_2_out_9), .in_8(and_gate_2_out_10), .out_12(D));  // open: in_1, in_2, in_3, in_4, in_5, in_6, out_9, out_10, out_11

  assign Z = X;
endmodule

module AND_GATE (
  input  in_1,
  input  in_2,
  input  in_3,
  input  in_4,
  input  in_5,
  input  in_6,
  input  in_7,
  input  in_8,
  output out_9,
  output out_10,
  output out_11,
  output out_12
);

  and and_1 (out_9, in_1, in_2);
  and and_2 (out_10, in_3, in_4);
  and and_3 (out_11, in_5, in_6);
  and and_4 (out_12, in_7, in_8);
endmodule

module OR_GATE (
  input  in_1,
  input  in_2,
  input  in_3,
  input  in_4,
  input  in_5,
  input  in_6,
  input  in_7,
  input  in_8,
  output out_9,
  output out_10,
  output out_11,
  output out_12
);

  or or_1 (out_9, in_1, in_2);
  or or_2 (out_10, in_3, in_4);
  or or_3 (out_11, in_5, in_6);
  or or_4 (out_12, in_7, in_8);
endmodule

module NOT_GATE (
  input  in_1,
  input  in_2,
  input  in_3,
  input  in_4,
  input  in_5,
  input  in_6,
  output out_7,
  output out_8,
  output out_9,
  output out_10,
  output out_11,
  output out_12
);

  not not_1 (out_7, in_1);
  not not_2 (out_8, in_2);
  not not_3 (out_9, in_3);
  not not_4 (out_10, in_4);
  not not_5 (out_11, in_5);
  not not_6 (out_12, in_6);
endmodule
