// Logisim project lab 3.circ as structural Verilog: 4 circuits, main circuit main
module main (
  input  A,
  input  B,
  input  C,
  output out_4
);

  wire ic_7404_not_gate_1_p1, ic_7404_not_gate_1_p3, ic_7404_not_gate_1_p5, ic_7411_and_gate_1_out_10,
       ic_7411_and_gate_1_out_11, ic_7411_and_gate_1_out_12;

  // IC_7404_NOT_GATE ic_7404_not_gate_1: pin names not known; wires that end beside it: ic_7404_not_gate_1_p1, C, ic_7404_not_gate_1_p3, B, ic_7404_not_gate_1_p5, A
  IC_7411_AND_GATE ic_7411_and_gate_1 (
    .in_1(ic_7404_not_gate_1_p1), .in_2(B), .in_3(A), .in_4(ic_7404_not_gate_1_p1), .in_5(B),
    .in_6(ic_7404_not_gate_1_p5), .in_7(C), .in_8(ic_7404_not_gate_1_p3), .in_9(ic_7404_not_gate_1_p5),
    .out_10(ic_7411_and_gate_1_out_10), .out_11(ic_7411_and_gate_1_out_11), .out_12(ic_7411_and_gate_1_out_12));
  IC_4075_OR_GATE ic_4075_or_gate_1 (
    .in_7(ic_7411_and_gate_1_out_10), .in_8(ic_7411_and_gate_1_out_11), .in_9(ic_7411_and_gate_1_out_12),
    .out_12(out_4));  // open: in_1, in_2, in_3, in_4, in_5, in_6, out_10, out_11
endmodule

module IC_7404_NOT_GATE (
  input  in_1,
  input  in_2,
  input  in_3,
  input  in_4,
  input  in_5,
  input  in_6,
  output out_7,
  output out_8,
  output out_9,
  output out_10,
  output out_11,
  output out_12
);

  not not_1 (out_7, in_1);
  not not_2 (out_8, in_2);
  not not_3 (out_9, in_3);
  not not_4 (out_10, in_4);
  not not_5 (out_11, in_5);
  not not_6 (out_12, in_6);
endmodule

module IC_4075_OR_GATE (
  input  in_1,
  input  in_2,
  input  in_3,
  input  in_4,
  input  in_5,
  input  in_6,
  input  in_7,
  input  in_8,
  input  in_9,
  output out_10,
  output out_11,
  output out_12
);

  or or_1 (out_10, in_1, in_2, in_3);
  or or_2 (out_11, in_4, in_5, in_6);
  or or_3 (out_12, in_7, in_8, in_9);
endmodule

module IC_7411_AND_GATE (
  input  in_1,
  input  in_2,
  input  in_3,
  input  in_4,
  input  in_5,
  input  in_6,
  input  in_7,
  input  in_8,
  input  in_9,
  output out_10,
  output out_11,
  output out_12
);

  and and_1 (out_10, in_1, in_2, in_3);
  and and_2 (out_11, in_4, in_5, in_6);
  and and_3 (out_12, in_7, in_8, in_9);
endmodule
