// Logisim project week 4.circ as structural Verilog: 4 circuits, main circuit main
module main (
  input  W,
  input  X,
  input  y,
  input  Z,
  output out_5,
  output out_6,
  output out_7,
  output out_8
);

  wire n4075_or_2_out_11, n4075_or_2_out_12, n7404_not_1_out_8, n7404_not_1_out_11, n7411_and_1_out_10,
       n7411_and_1_out_11, n7411_and_2_out_10, n7411_and_2_out_11, n7411_and_3_out_10, n7411_and_3_out_11,
       n7411_and_3_out_12, undriven;

  _7404_not u_7404_not_1 (
    .in_6(y), .out_8(n7404_not_1_out_8), .out_11(n7404_not_1_out_11), .out_12(X));  // open: in_1, in_2, in_3, in_4, in_5, out_7, out_9, out_10
  _7411_AND u_7411_and_1 (
    .in_1(Z), .in_2(X), .in_3(X), .in_4(y), .in_5(y), .in_6(X), .out_10(n7411_and_1_out_10),
    .out_11(n7411_and_1_out_11));  // open: in_7, in_8, in_9, out_12
  _4075_or u_4075_or_1 (
    .in_7(n7411_and_1_out_10), .in_8(n7411_and_1_out_11), .in_9(W), .out_12(out_7));  // open: in_1, in_2, in_3, in_4, in_5, in_6, out_10, out_11
  _7411_AND u_7411_and_2 (
    .in_1(Z), .in_2(undriven), .in_3(undriven), .in_4(n7404_not_1_out_8), .in_5(n7404_not_1_out_8),
    .in_6(n7404_not_1_out_8), .out_10(n7411_and_2_out_10), .out_11(n7411_and_2_out_11));  // open: in_7, in_8, in_9, out_12
  _7411_AND u_7411_and_3 (
    .in_1(n7404_not_1_out_8), .in_2(n7404_not_1_out_8), .in_3(X), .in_5(y), .in_7(Z),
    .out_10(n7411_and_3_out_10), .out_11(n7411_and_3_out_11), .out_12(n7411_and_3_out_12));  // open: in_4, in_6, in_8, in_9
  _4075_or u_4075_or_2 (
    .in_4(n7411_and_2_out_10), .in_5(n7411_and_2_out_11), .in_6(n7411_and_2_out_10),
    .in_7(n7411_and_3_out_10), .in_8(n7411_and_3_out_11), .in_9(n7411_and_3_out_12),
    .out_11(n4075_or_2_out_11), .out_12(n4075_or_2_out_12));  // open: in_1, in_2, in_3, out_10
endmodule

module _7411_AND (
  input  in_1,
  input  in_2,
  input  in_3,
  input  in_4,
  input  in_5,
  input  in_6,
  input  in_7,
  input  in_8,
  input  in_9,
  output out_10,
  output out_11,
  output out_12
);

  and and_1 (out_10, in_1, in_2, in_3);
  and and_2 (out_11, in_4, in_5, in_6);
  and and_3 (out_12, in_7, in_8, in_9);
endmodule

module _4075_or (
  input  in_1,
  input  in_2,
  input  in_3,
  input  in_4,
  input  in_5,
  input  in_6,
  input  in_7,
  input  in_8,
  input  in_9,
  output out_10,
  output out_11,
  output out_12
);

  or or_1 (out_10, in_1, in_2, in_3);
  or or_2 (out_11, in_4, in_5, in_6);
  or or_3 (out_12, in_7, in_8, in_9);
endmodule

module _7404_not (
  input  in_1,
  input  in_2,
  input  in_3,
  input  in_4,
  input  in_5,
  input  in_6,
  output out_7,
  output out_8,
  output out_9,
  output out_10,
  output out_11,
  output out_12
);

  not not_1 (out_7, in_1);
  not not_2 (out_8, in_2);
  not not_3 (out_9, in_3);
  not not_4 (out_10, in_4);
  not not_5 (out_11, in_5);
  not not_6 (out_12, in_6);
endmodule
