// Logisim project week 5 part1.circ as structural Verilog: 2 circuits, main circuit ripple caryy adder
module ripple_caryy_adder (
  input  Cin,
  input  A,
  input  B,
  output S,
  output Cout
);

  wire and_1_out, and_2_out, xor_1_out;

  xor xor_1 (xor_1_out, A, B);
  xor xor_2 (S, xor_1_out, Cin);
  and and_1 (and_1_out, Cin, xor_1_out);
  and and_2 (and_2_out, B, A);
  or or_1 (Cout, and_1_out, and_2_out);
endmodule

// 4 bit adder subtractor
module main (
  input  [3:0] A,
  input  [3:0] B,
  input  Mode,
  output [3:0] SUM,
  output Carry_out
);

  wire ripple_caryy_adder_1_cout, ripple_caryy_adder_2_cout, ripple_caryy_adder_3_cout, xor_1_out, xor_2_out,
       xor_3_out, xor_4_out;

  xor xor_1 (xor_1_out, B[0], Mode);
  xor xor_2 (xor_2_out, B[1], Mode);
  xor xor_3 (xor_3_out, B[2], Mode);
  xor xor_4 (xor_4_out, B[3], Mode);
  ripple_caryy_adder ripple_caryy_adder_1 (
    .Cin(Mode), .A(A[0]), .B(xor_1_out), .S(SUM[0]), .Cout(ripple_caryy_adder_1_cout));
  ripple_caryy_adder ripple_caryy_adder_2 (
    .Cin(ripple_caryy_adder_1_cout), .A(A[1]), .B(xor_2_out), .S(SUM[1]), .Cout(ripple_caryy_adder_2_cout));
  ripple_caryy_adder ripple_caryy_adder_3 (
    .Cin(ripple_caryy_adder_2_cout), .A(A[2]), .B(xor_3_out), .S(SUM[2]), .Cout(ripple_caryy_adder_3_cout));
  ripple_caryy_adder ripple_caryy_adder_4 (
    .Cin(ripple_caryy_adder_3_cout), .A(A[3]), .B(xor_4_out), .S(SUM[3]), .Cout(Carry_out));
endmodule
