// Logisim project week 5 part2.circ as structural Verilog: 2 circuits, main circuit main
module main (
  input  in_1,
  input  A1,
  input  B1,
  input  A2,
  input  B2,
  input  A3,
  input  B3,
  input  A4,
  input  B4,
  output S1,
  output S2,
  output S3,
  output S4,
  output out_14
);

  wire adder_1_cout, adder_2_cout, adder_3_cout;

  Adder #(.width(1)) adder_1 (.a(A1), .b(B1), .out(S1), .cin(in_1), .cout(adder_1_cout));
  Adder #(.width(1)) adder_2 (.a(A2), .b(B2), .out(S2), .cin(adder_1_cout), .cout(adder_2_cout));
  Adder #(.width(1)) adder_3 (.a(A3), .b(B3), .out(S3), .cin(adder_2_cout), .cout(adder_3_cout));
  Adder #(.width(1)) adder_4 (.a(A4), .b(B4), .out(S4), .cin(adder_3_cout), .cout(out_14));
endmodule

module BCD (
  input  in_1,
  input  in_2,
  input  in_3,
  input  in_4,
  input  in_5,
  input  in_6,
  input  in_7,
  input  in_8,
  input  in_9,
  output out_10,
  output out_11,
  output out_12,
  output out_13,
  output out_14
);

  wire and_1_out, and_2_out, main_1_out_14, main_1_s1, main_1_s2, main_1_s3, main_1_s4, or_1_out;

  main main_1 (
    .in_1(in_1), .A1(in_2), .B1(in_3), .A2(in_4), .B2(in_5), .A3(in_6), .B3(in_7), .A4(in_8), .B4(in_9),
    .S1(main_1_s1), .S2(main_1_s2), .S3(main_1_s3), .S4(main_1_s4), .out_14(main_1_out_14));
  and and_1 (and_1_out, main_1_s1, main_1_s2);
  or or_1 (or_1_out, and_1_out, and_2_out);
  or or_2 (out_14, main_1_out_14, or_1_out);
  and and_2 (and_2_out, main_1_s3, main_1_s1);
  main main_2 (
    .in_1(out_14), .A1(out_14), .B1(out_14), .A2(out_14), .B2(main_1_s1), .A3(main_1_s2), .B3(main_1_s3),
    .A4(main_1_s4), .S1(out_10), .S2(out_11), .S3(out_12), .S4(out_13));  // open: B4, out_14
  // also tied to GND on the sheet: out_14

  // Notes on the sheet:
  //   s1
  //   s2
  //   s3
  //   s4
  //   Cout
  //   C(BCD CARRY)
endmodule
